# Fritzing sketch Ηρεμίξ (saved by Fritzing 0.9.3b)
breadboards: 1

parts:
  DFPlayer_Mini1 = DFPlayer MINI [package="DIP (Dual Inline) [THT]"]  # not connected
  SP1 = SPEAKER [package=pcb_mount_speaker]  # not connected
  Εξάρτημα1 = Arduino Uno (Rev3)
  R1 = Resistor [tolerance=±5% resistance=220 package=THT]
  S1 = Square Pushbutton
  S2 = Square Pushbutton
  S3 = Square Pushbutton
  S4 = Square Pushbutton
  Εξάρτημα2 = 8BIT LED RING [part_number=1643]

nets:
  N1: Εξάρτημα1.D9_PWM, R1.Pin_1
  N2: Εξάρτημα1.D10_PWM/SS, R1.Pin_0
  N3: Εξάρτημα1.D13/SCK, Εξάρτημα2.GND
  N4: Εξάρτημα1.D2, S4.leg1
  N5: Εξάρτημα1.D3_PWM, S3.leg1
  N6: Εξάρτημα1.D4, S2.leg1
  N7: S1.leg0, S2.leg0, S3.leg0, S4.leg0

custom parts:
  DFPlayer MINI: MP3 module by DFRobot.com for playing Music from an SD-Card. Supports WAV and MP3 files.
  8BIT LED RING: 8Bit LED ring
